// Logisim project test.circ as structural Verilog: 1 circuit, main circuit main
module main (
  input  [7:0] in_1,
  input  [7:0] in_2
);

  wire clock_1_out, dipswitch_1_p1, dipswitch_1_p2;
  wire [7:0] ram_1_dout;

  Clock clock_1 (.out(clock_1_out));
  // DipSwitch #(.number(2)) dipswitch_1: pin names not known; wires that end beside it: dipswitch_1_p1, dipswitch_1_p2
  RAM ram_1 (.addr(in_1), .we(dipswitch_1_p1), .oe(dipswitch_1_p2), .clk(clock_1_out), .din(in_2), .dout(ram_1_dout));
  LedBar ledbar_1 (
    .led0(ram_1_dout[0]), .led1(ram_1_dout[1]), .led2(ram_1_dout[2]), .led3(ram_1_dout[3]),
    .led4(ram_1_dout[4]), .led5(ram_1_dout[5]), .led6(ram_1_dout[6]), .led7(ram_1_dout[7]));
endmodule
